// Logisim project fweoiejfoiwjef.circ as structural Verilog: 7 circuits, main circuit main
module main (
  input  [15:0] A,
  input  [3:0] B,
  input  [7:0] in_3,
  output [15:0] out_4,
  output out_5,
  output [7:0] out_6
);

  rotr rotr_1 (.in_1(A), .in_2(B), .out_3(out_4));
  Ex4 ex4_1 (.In1(in_3), .Out1(out_5), .Out2(out_6));
endmodule

module Ex4 (
  input  [7:0] In1,
  output Out1,
  output [7:0] Out2
);

  and and_1 (Out1, In1[0], In1[7]);
  not not_1 (Out2[7], In1[7]);

  assign Out2[6:0] = In1[6:0];
endmodule

module rotr (
  input  [15:0] in_1,
  input  [3:0] in_2,
  output [15:0] out_3
);

  wire [15:0] inputashift1circuit_1_outputshift1, inputashift2circuit_1_outputshift2,
       inputashift4circuit_1_outputshift4, inputashift8circuit_1_outputshift8, multiplexer_1_out,
       multiplexer_2_out, multiplexer_3_out;

  Multiplexer #(.width(16), .enable("false")) multiplexer_1 (
    .in0(in_1), .in1(inputashift1circuit_1_outputshift1), .out(multiplexer_1_out), .sel(in_2[0]));
  Multiplexer #(.width(16), .enable("false")) multiplexer_2 (
    .in0(multiplexer_1_out), .in1(inputashift2circuit_1_outputshift2), .out(multiplexer_2_out), .sel(in_2[1]));
  Multiplexer #(.width(16), .enable("false")) multiplexer_3 (
    .in0(multiplexer_2_out), .in1(inputashift4circuit_1_outputshift4), .out(multiplexer_3_out), .sel(in_2[2]));
  Multiplexer #(.width(16), .enable("false")) multiplexer_4 (
    .in0(multiplexer_3_out), .in1(inputashift8circuit_1_outputshift8), .out(out_3), .sel(in_2[3]));
  InputAShift8Circuit inputashift8circuit_1 (
    .in_1(multiplexer_3_out), .OutputShift8(inputashift8circuit_1_outputshift8));
  InputAShift4Circuit inputashift4circuit_1 (
    .in_1(multiplexer_2_out), .OutputShift4(inputashift4circuit_1_outputshift4));
  InputAShift2Circuit inputashift2circuit_1 (
    .in_1(multiplexer_1_out), .OutputShift2(inputashift2circuit_1_outputshift2));
  InputAShift1Circuit inputashift1circuit_1 (.in_1(in_1), .OutputShift1(inputashift1circuit_1_outputshift1));

  // Other names for the same wires on the sheet: InputA[15:0] = in_1
endmodule

module InputAShift1Circuit (
  input  [15:0] in_1,
  output [15:0] OutputShift1
);


  assign OutputShift1 = {in_1[14:0], in_1[15]};
endmodule

module InputAShift2Circuit (
  input  [15:0] in_1,
  output [15:0] OutputShift2
);


  assign OutputShift2 = {in_1[13:0], in_1[15:14]};
endmodule

module InputAShift4Circuit (
  input  [15:0] in_1,
  output [15:0] OutputShift4
);


  assign OutputShift4 = {in_1[11:0], in_1[15:12]};
endmodule

module InputAShift8Circuit (
  input  [15:0] in_1,
  output [15:0] OutputShift8
);


  assign OutputShift8 = {in_1[7:0], in_1[15:8]};
endmodule
