// Logisim project part1.2.circ as structural Verilog: 6 circuits, main circuit NAND1
module main (
  output [7:0] out_1,
  output [7:0] out_2
);

  AddMachine addmachine_1 (.out_1(out_1), .out_2(out_2));
endmodule

module NAND1 (
  input  in_1,
  input  in_2,
  output out_3
);

  wire and_1_out;

  and and_1 (and_1_out, in_1, in_2);
  not not_1 (out_3, and_1_out);
endmodule

module NOR1 (
  input  in_1,
  input  in_2,
  output out_3
);

  wire or_1_out;

  or or_1 (or_1_out, in_1, in_2);
  not not_1 (out_3, or_1_out);
endmodule

module TWOTOONEMUX (
  input  A,
  input  x,
  input  B,
  output out_4
);

  wire nand1_1_out_3, nand1_2_out_3, nand1_3_out_3;

  NAND1 nand1_1 (.in_1(x), .in_2(x), .out_3(nand1_1_out_3));
  NAND1 nand1_2 (.in_1(A), .in_2(x), .out_3(nand1_2_out_3));
  NAND1 nand1_3 (.in_1(nand1_1_out_3), .in_2(B), .out_3(nand1_3_out_3));
  NAND1 nand1_4 (.in_1(nand1_2_out_3), .in_2(nand1_3_out_3), .out_3(out_4));
endmodule

module FOURTOONEMUX (
  input  A,
  input  B,
  input  x,
  input  C,
  input  D,
  input  y,
  output out_7
);

  wire twotoonemux_1_out_4, twotoonemux_2_out_4;

  TWOTOONEMUX twotoonemux_1 (.A(A), .x(B), .B(x), .out_4(twotoonemux_1_out_4));
  TWOTOONEMUX twotoonemux_2 (.A(C), .x(D), .B(x), .out_4(twotoonemux_2_out_4));
  TWOTOONEMUX twotoonemux_3 (.A(twotoonemux_1_out_4), .x(twotoonemux_2_out_4), .B(y), .out_4(out_7));
endmodule

module AddMachine (
  output [7:0] out_1,
  output [7:0] out_2
);

  wire clock_1_out;

  Adder adder_1 (.a(8'h1), .b(out_2), .out(out_1));  // open: cin, cout
  Register register_1 (.D(out_1), .clk(clock_1_out), .Q(out_2));  // open: en, clr
  Clock clock_1 (.out(clock_1_out));
endmodule
